# Fritzing sketch SensorFinal (1) (saved by Fritzing 0.9.3b)
breadboards: 1

parts:
  C1 = Capacitor [package=cap-pth-small2]
  C2 = Capacitor [package=cap-pth-small2]
  XTAL1 = Crystal [frequency="16 Mhz" package=THT]
  Q1 = TRANSISTOR_NPN [package=to-92]
  U1 = TRANSISTOR_NPN_2 [package=to-92]
  R2 = Resistor [package="2010 [SMD]"]
  R3 = Resistor [package="2010 [SMD]"]
  R4 = Resistor [tolerance=±5% resistance=220 package=THT]
  R5 = Resistor [tolerance=±5% resistance=220 package=THT]
  R6 = Resistor [tolerance=±5% resistance=220 package=THT]
  L1 = Inductor [package="0603 [SMD]"]
  Q2 = NPN-Transistor [package="TO92 [THT]"]
  R7 = Resistor [tolerance=±5% resistance=220 package=THT]

nets:
  N1: C1.1, C2.1, C2.2, U1.B
  N2: C1.2, XTAL1.pin_0, XTAL1.pin_1, Q1.B, R3.Pin_0, R3.Pin_1, R4.Pin_0, R5.Pin_0
  N3: Q1.E, R2.Pin_0, R2.Pin_1
  N4: U1.E, R4.Pin_1
  N5: R6.Pin_1, L1.pin_0
  N6: Q2.C, R7.Pin_1

notes:
  GND
  To Analog
  Pin
  5V
  V-out
  High Frequency
  12V
  Inductor will be embedded in the road
