# Fritzing sketch master (saved by Fritzing 0.8.7b)

parts:
  Part7 = Arduino Uno (Rev3)
  Part8 = NRF24L01

nets:
  N1: Part7.D9_PWM, Part8.CE
  N2: Part7.D10_PWM/SS, Part8.CSN
  N3: Part7.D11_PWM/MOSI, Part8.MOSI
  N4: Part7.D12/MISO, Part8.MISO
  N5: Part7.D13/SCK, Part8.SCK
  5V: Part7.5V, Part8.VCC
  GND: Part7.GND, Part8.GND
